# Fritzing sketch Sketch of project (saved by Fritzing 0.9.3b)
breadboards: 1

parts:
  Part1 = Arduino Uno (Rev3)
  Part2 = Bluetooth HC-05 Macho
  DHT1 = DHT22 Humidity and Temperature Sensor
  hc-sr1 = hc-sr04

nets:
  N1: Part1.A0, DHT1.DATA
  N2: Part1.D8, hc-sr1.Trig
  N3: Part1.D9_PWM, hc-sr1.Echo
  N4: Part1.D0/RX, Part2.RXD
  N5: Part1.D1/TX, Part2.TXD
  VCC: Part1.5V, Part2.VCC, DHT1.VDD, hc-sr1.VCC
  GND: Part1.GND, Part2.GND, DHT1.GND, hc-sr1.GND

notes:
  HC-SR04
  TRIG : 8
  ECHO : 9
  HC-05
  TXD : 0
  RXD : 1
  DHT-22
  DATA : A0

// code stored in the sketch: Untitled2.ino
#include "dht.h"
#include <SoftwareSerial.h>
#define dht_apin A0 // Analog Pin sensor is connected to
#define trigPin 8
#define echoPin 9
 
dht DHT;

// defines variables
long duration;
int distance;
void setup() {
  pinMode(trigPin, OUTPUT); // Sets the trigPin as an Output
  pinMode(echoPin, INPUT); // Sets the echoPin as an Input
  delay(500);//Wait for system to boot up
  Serial.println("DHT11 Humidity & temperature Sensor\n\n");
  Serial.begin(9600); // Starts the serial communication
  delay(1000);//Wait before accessing the sensor
}
void loop() {
  // Clears the trigPin
  digitalWrite(trigPin, LOW);
  delayMicroseconds(2);
  // Sets the trigPin on HIGH state for 10 micro seconds
  digitalWrite(trigPin, HIGH);
  delayMicroseconds(10);
  digitalWrite(trigPin, LOW);
  // Reads the echoPin, returns the sound wave travel time in microseconds
  duration = pulseIn(echoPin, HIGH);
  // Calculating the distance
  distance = (duration/2) / 29.1;  
  // Prints the distance on the Serial Monitor
  Serial.print("Distance: ");
  Serial.print(distance);
  Serial.println(" cm");
  DHT.read11(dht_apin);
  Serial.print("Current humidity = ");
  Serial.print(DHT.humidity);
  Serial.print("%  ");
  Serial.print("temperature = ");
  Serial.print(DHT.temperature); 
  Serial.println("C  ");
  //delay(3000);// Must wait at least 3 seconds before accessing DHT11
}
